// Logisim project L08_PT02_B.circ as structural Verilog: 1 circuit, main circuit main
module main (
  input  D,
  input  Gate,
  output Q,
  output Q_prime
);

  wire nand_1_out, nand_2_out, nand_3_out;

  nand nand_1 (nand_1_out, D, D);
  nand nand_2 (nand_2_out, D, Gate);
  nand nand_3 (nand_3_out, nand_1_out, Gate);
  or or_1 (Q, ~Q_prime, ~nand_2_out);  // OR_Gate
  or or_2 (Q_prime, ~nand_3_out, ~Q);  // OR_Gate
endmodule
