// Logisim project SSI-7400-replace.circ as structural Verilog: 5 circuits, main circuit main
module main (
  input  A,
  input  B,
  input  C,
  input  D,
  output out_5
);

  _7408 u_7408_1 ();  // open: _1__1A, _2__1B, _3__1Y, _4__2A, _5__2B, _6__2Y, _7__GND, _14__Vcc, _13__4B, _12__4A, _11__4Y, _10__3B, _9__3A, _8__3Y
  _7404 u_7404_1 ();  // open: _1__1A, _2__1Y, _3__2A, _4__2Y, _5__3A, _6__3Y, _7__GND, _14__Vcc, _13__6A, _12__6Y, _11__5A, _10__5Y, _9__4A, _8__4Y
  _7432 u_7432_1 ();  // open: _1__1A, _2__1B, _3__1Y, _4__2A, _5__2B, _6__2Y, _7__GND, _14__Vcc, _13__4B, _12__4A, _11__4Y, _10__3B, _9__3A, _8__3Y
endmodule

module _7400 (
  input  _1__1A,
  input  _14__Vcc,
  input  _2__1B,
  input  _13__4B,
  input  _12__4A,
  input  _4__2A,
  input  _5__2B,
  input  _10__3B,
  input  _9__3A,
  input  _7__GND,
  output _3__1Y,
  output _11__4Y,
  output _6__2Y,
  output _8__3Y
);

  nand nand_1 (_3__1Y, _2__1B, _1__1A);
  nand nand_2 (_6__2Y, _5__2B, _4__2A);
  nand nand_3 (_11__4Y, _13__4B, _12__4A);
  nand nand_4 (_8__3Y, _10__3B, _9__3A);

  // Notes on the sheet:
  //   7400: quad NAND
endmodule

module _7404 (
  input  _1__1A,
  input  _14__Vcc,
  input  _13__6A,
  input  _3__2A,
  input  _11__5A,
  input  _5__3A,
  input  _9__4A,
  input  _7__GND,
  output _2__1Y,
  output _12__6Y,
  output _4__2Y,
  output _10__5Y,
  output _6__3Y,
  output _8__4Y
);

  not not_1 (_2__1Y, _1__1A);
  not not_2 (_4__2Y, _3__2A);
  not not_3 (_6__3Y, _5__3A);
  not not_4 (_12__6Y, _13__6A);
  not not_5 (_10__5Y, _11__5A);
  not not_6 (_8__4Y, _9__4A);

  // Notes on the sheet:
  //   7404: hex inverter
endmodule

module _7408 (
  input  _1__1A,
  input  _14__Vcc,
  input  _2__1B,
  input  _13__4B,
  input  _12__4A,
  input  _4__2A,
  input  _5__2B,
  input  _10__3B,
  input  _9__3A,
  input  _7__GND,
  output _3__1Y,
  output _11__4Y,
  output _6__2Y,
  output _8__3Y
);

  and and_1 (_3__1Y, _2__1B, _1__1A);
  and and_2 (_6__2Y, _5__2B, _4__2A);
  and and_3 (_11__4Y, _13__4B, _12__4A);
  and and_4 (_8__3Y, _10__3B, _9__3A);

  // Notes on the sheet:
  //   7408: quad AND
endmodule

module _7432 (
  input  _1__1A,
  input  _14__Vcc,
  input  _2__1B,
  input  _13__4B,
  input  _12__4A,
  input  _4__2A,
  input  _5__2B,
  input  _10__3B,
  input  _9__3A,
  input  _7__GND,
  output _3__1Y,
  output _11__4Y,
  output _6__2Y,
  output _8__3Y
);

  or or_1 (_3__1Y, _2__1B, _1__1A);
  or or_2 (_6__2Y, _5__2B, _4__2A);
  or or_3 (_11__4Y, _13__4B, _12__4A);
  or or_4 (_8__3Y, _10__3B, _9__3A);

  // Notes on the sheet:
  //   7432: quad OR
endmodule
