// Logisim project final.circ as structural Verilog
// Adder
module Full_Adder (
  input  A,
  input  B,
  input  Cin,
  output Sum,
  output Cout
);

  wire and_1_out, and_2_out, and_3_out;

  xor xor_1 (Sum, A, B, Cin);
  and and_1 (and_1_out, B, A);
  and and_2 (and_2_out, B, Cin);
  and and_3 (and_3_out, A, Cin);
  or or_1 (Cout, and_1_out, and_2_out, and_3_out);
endmodule

module _4_Bit_Adder (
  input  in_1,
  input  in_2,
  input  in_3,
  input  in_4,
  input  in_5,
  input  in_6,
  input  in_7,
  input  in_8,
  output out_9,
  output out_10,
  output out_11,
  output out_12
);

  wire full_adder_1_cout, full_adder_2_cout, full_adder_3_cout;

  Full_Adder full_adder_1 (.A(in_1), .B(in_2), .Sum(out_9), .Cout(full_adder_1_cout), .Cin(1'b0));
  Full_Adder full_adder_2 (.A(in_3), .B(in_4), .Sum(out_10), .Cout(full_adder_2_cout), .Cin(full_adder_1_cout));
  Full_Adder full_adder_3 (.A(in_5), .B(in_6), .Sum(out_11), .Cout(full_adder_3_cout), .Cin(full_adder_2_cout));
  Full_Adder full_adder_4 (.A(in_7), .B(in_8), .Sum(out_12), .Cin(full_adder_3_cout));  // open: Cout
endmodule

// 1-Bit Reg
module _1_Bit_Register (
  input  D,
  input  WE,
  input  Clock,
  output Q
);

  wire multiplexer_1_out;

  Multiplexer #(.enable("false")) multiplexer_1 (.in0(Q), .in1(D), .out(multiplexer_1_out), .sel(WE));
  D_Flip_Flop d_ff_1 (.clk(Clock), .D(multiplexer_1_out), .Q(Q));  // open: Qn, preset, en, reset
endmodule

// 4-Bir Reg
module _4_Bit_Register (
  input  [3:0] in_1,
  input  WE,
  input  Clock,
  output [3:0] out_4
);

  _1_Bit_Register u_1_bit_register_1 (.D(in_1[3]), .Q(out_4[3]), .WE(WE), .Clock(Clock));
  _1_Bit_Register u_1_bit_register_2 (.D(in_1[2]), .Q(out_4[2]), .WE(WE), .Clock(Clock));
  _1_Bit_Register u_1_bit_register_3 (.D(in_1[1]), .Q(out_4[1]), .WE(WE), .Clock(Clock));
  _1_Bit_Register u_1_bit_register_4 (.D(in_1[0]), .Q(out_4[0]), .WE(WE), .Clock(Clock));
endmodule

module Write_Decoder (
  input  Clock_Input,
  output [2:0] out_2
);

  wire d_ff_1_qn, d_ff_2_qn, d_ff_3_qn, nand_1_out, nand_2_out, nand_3_out, nand_4_out, nand_5_out,
       nand_6_out, nand_7_out;

  D_Flip_Flop d_ff_1 (.clk(Clock_Input), .D(nand_3_out), .Q(out_2[2]), .Qn(d_ff_1_qn));  // open: preset, en, reset
  nand nand_1 (nand_1_out, out_2[2], d_ff_3_qn);
  nand nand_2 (nand_2_out, out_2[2], d_ff_2_qn);
  nand nand_3 (nand_3_out, nand_2_out, nand_1_out, nand_4_out);
  nand nand_4 (nand_4_out, d_ff_1_qn, out_2[0], out_2[1]);
  D_Flip_Flop d_ff_2 (.clk(Clock_Input), .D(nand_7_out), .Q(out_2[1]), .Qn(d_ff_2_qn));  // open: preset, en, reset
  nand nand_5 (nand_5_out, out_2[1], d_ff_3_qn);
  nand nand_6 (nand_6_out, d_ff_2_qn, out_2[0]);
  nand nand_7 (nand_7_out, nand_6_out, nand_5_out);
  D_Flip_Flop d_ff_3 (.clk(Clock_Input), .D(d_ff_3_qn), .Q(out_2[0]), .Qn(d_ff_3_qn));  // open: preset, en, reset
endmodule
