// Logisim project Lab_04_PT_05_4to1_MUX.circ as structural Verilog: 6 circuits, main circuit main
module main (
  input  A0,
  input  B0,
  input  A1,
  input  B1,
  input  A2,
  input  B2,
  input  A3,
  input  B3,
  input  S0,
  input  S1,
  output OUT_0,
  output OUT_1,
  output OUT_2,
  output OUT_3
);

  wire bit_wise_and_1_out_0, bit_wise_and_1_out_1, bit_wise_and_1_out_2, bit_wise_and_1_out_3,
       bit_wise_or_1_out_0, bit_wise_or_1_out_1, bit_wise_or_1_out_2, bit_wise_or_1_out_3,
       bit_wise_xor_1_out_0, bit_wise_xor_1_out_1, bit_wise_xor_1_out_2, bit_wise_xor_1_out_3,
       n4_bit_adder_1_out_9, n4_bit_adder_1_out_10, n4_bit_adder_1_out_11, n4_bit_adder_1_out_12;

  bit_wise_XOR bit_wise_xor_1 (
    .A0(A0), .A1(A1), .A2(A2), .A3(A3), .B0(B0), .B1(B1), .B2(B2), .B3(B3), .Out_0(bit_wise_xor_1_out_0),
    .Out_1(bit_wise_xor_1_out_1), .Out_2(bit_wise_xor_1_out_2), .Out_3(bit_wise_xor_1_out_3));
  bit_wise_AND bit_wise_and_1 (
    .A0(A0), .A1(A1), .A2(A2), .A3(A3), .B0(B0), .B1(B1), .B2(B2), .B3(B3), .Out_0(bit_wise_and_1_out_0),
    .Out_1(bit_wise_and_1_out_1), .Out_2(bit_wise_and_1_out_2), .Out_3(bit_wise_and_1_out_3));
  bit_wise_OR bit_wise_or_1 (
    .A0(A0), .A1(A1), .A2(A2), .A3(A3), .B0(B0), .B1(B1), .B2(B2), .B3(B3), .Out_0(bit_wise_or_1_out_0),
    .Out_1(bit_wise_or_1_out_1), .Out_2(bit_wise_or_1_out_2), .Out_3(bit_wise_or_1_out_3));
  _4_bit_Adder u_4_bit_adder_1 (
    .in_1(A0), .in_2(B0), .in_3(A1), .in_4(B1), .in_5(A2), .in_6(B2), .in_7(A3), .in_8(B3),
    .out_9(n4_bit_adder_1_out_9), .out_10(n4_bit_adder_1_out_10), .out_11(n4_bit_adder_1_out_11),
    .out_12(n4_bit_adder_1_out_12));
  Multiplexer #(.select(2), .enable("false")) multiplexer_1 (
    .in0(bit_wise_xor_1_out_0), .in1(bit_wise_and_1_out_0), .in2(bit_wise_or_1_out_0),
    .in3(n4_bit_adder_1_out_9), .out(OUT_0), .sel({S1, S0}));
  Multiplexer #(.select(2), .enable("false")) multiplexer_2 (
    .in0(bit_wise_xor_1_out_1), .in1(bit_wise_and_1_out_1), .in2(bit_wise_or_1_out_1),
    .in3(n4_bit_adder_1_out_10), .out(OUT_1), .sel({S1, S0}));
  Multiplexer #(.select(2), .enable("false")) multiplexer_3 (
    .in0(bit_wise_xor_1_out_2), .in1(bit_wise_and_1_out_2), .in2(bit_wise_or_1_out_2),
    .in3(n4_bit_adder_1_out_11), .out(OUT_2), .sel({S1, S0}));
  Multiplexer #(.select(2), .enable("false")) multiplexer_4 (
    .in0(bit_wise_xor_1_out_3), .in1(bit_wise_and_1_out_3), .in2(bit_wise_or_1_out_3),
    .in3(n4_bit_adder_1_out_12), .out(OUT_3), .sel({S1, S0}));

  // Notes on the sheet:
  //   S0' S1' = XOR
  //   S0 S1' = OR
  //   S0' S1 = AND
  //   S0 S1 = Add
endmodule

module Full_Adder (
  input  A,
  input  B,
  input  Cin,
  output Sum,
  output Cout
);

  wire and_1_out, and_2_out, and_3_out;

  xor xor_1 (Sum, A, B, Cin);
  and and_1 (and_1_out, B, A);
  and and_2 (and_2_out, B, Cin);
  and and_3 (and_3_out, A, Cin);
  or or_1 (Cout, and_1_out, and_2_out, and_3_out);
endmodule

module bit_wise_AND (
  input  A0,
  input  A1,
  input  A2,
  input  A3,
  input  B0,
  input  B1,
  input  B2,
  input  B3,
  output Out_0,
  output Out_1,
  output Out_2,
  output Out_3
);

  and and_1 (Out_0, A0, B0);
  and and_2 (Out_1, A1, B1);
  and and_3 (Out_2, A2, B2);
  and and_4 (Out_3, A3, B3);
endmodule

module bit_wise_OR (
  input  A0,
  input  A1,
  input  A2,
  input  A3,
  input  B0,
  input  B1,
  input  B2,
  input  B3,
  output Out_0,
  output Out_1,
  output Out_2,
  output Out_3
);

  or or_1 (Out_0, A0, B0);
  or or_2 (Out_1, A1, B1);
  or or_3 (Out_2, A2, B2);
  or or_4 (Out_3, A3, B3);
endmodule

module bit_wise_XOR (
  input  A0,
  input  A1,
  input  A2,
  input  A3,
  input  B0,
  input  B1,
  input  B2,
  input  B3,
  output Out_0,
  output Out_1,
  output Out_2,
  output Out_3
);

  xor xor_1 (Out_0, A0, B0);
  xor xor_2 (Out_1, A1, B1);
  xor xor_3 (Out_2, A2, B2);
  xor xor_4 (Out_3, A3, B3);
endmodule

module _4_bit_Adder (
  input  in_1,
  input  in_2,
  input  in_3,
  input  in_4,
  input  in_5,
  input  in_6,
  input  in_7,
  input  in_8,
  output out_9,
  output out_10,
  output out_11,
  output out_12
);

  wire full_adder_1_cout, full_adder_2_cout, full_adder_3_cout;

  Full_Adder full_adder_1 (.A(in_1), .B(in_2), .Sum(out_9), .Cout(full_adder_1_cout), .Cin(1'b0));
  Full_Adder full_adder_2 (.A(in_3), .B(in_4), .Sum(out_10), .Cout(full_adder_2_cout), .Cin(full_adder_1_cout));
  Full_Adder full_adder_3 (.A(in_5), .B(in_6), .Sum(out_11), .Cout(full_adder_3_cout), .Cin(full_adder_2_cout));
  Full_Adder full_adder_4 (.A(in_7), .B(in_8), .Sum(out_12), .Cin(full_adder_3_cout));  // open: Cout
endmodule
