// Logisim project SR_SC_D_Latches-replace.circ as structural Verilog: 1 circuit, main circuit main
module main (
  input  S,
  input  R,
  input  S_2,
  input  R_2,
  input  D,
  input  Gate,
  output Q1_prime,
  output Q1,
  output Q2_prime,
  output Q2,
  output Q3_prime,
  output Q3
);


  assign Q1 = R;
  assign Q1_prime = S;
  assign Q2 = R_2;
  assign Q2_prime = S_2;
  assign Q3 = Gate;
  assign Q3_prime = D;

  // Notes on the sheet:
  //   NOR Latch
  //   NAND Latch
  //   Gated D Latch
endmodule
