// Logisim project Ring_Counter-replace.circ as structural Verilog: 1 circuit, main circuit main
module main (
  input  Clock_Input,
  input  Reset,
  output Out_0,
  output Out_1,
  output Out_2
);


  assign Out_0 = Clock_Input;
  assign Out_1 = Clock_Input;
  assign Out_2 = Reset;
endmodule
