// Logisim project L10_PT02_C.circ as structural Verilog: 1 circuit, main circuit main
module main (
  input  Clock_Input,
  output Out_0,
  output Out_1,
  output Out_2
);

  wire d_ff_1_qn, d_ff_2_qn;

  D_Flip_Flop d_ff_1 (.clk(Clock_Input), .D(Out_0), .Q(Out_2), .Qn(d_ff_1_qn));  // open: preset, en, reset
  D_Flip_Flop d_ff_2 (.clk(Clock_Input), .D(d_ff_1_qn), .Q(Out_1), .Qn(d_ff_2_qn));  // open: preset, en, reset
  D_Flip_Flop d_ff_3 (.clk(Clock_Input), .D(d_ff_2_qn), .Q(Out_0));  // open: Qn, preset, en, reset
endmodule
