// Logisim project Lab_05_PT_07_latches.circ as structural Verilog: 1 circuit, main circuit main
module main (
  input  S,
  input  R,
  input  R_2,
  input  S_2,
  input  D,
  input  Gate,
  output Q1_prime,
  output Q1,
  output Q2_prime,
  output Q2,
  output Q3_prime,
  output Q3
);

  wire and_1_out, and_2_out, not_1_out;

  not not_1 (not_1_out, D);
  and and_1 (and_1_out, D, Gate);
  and and_2 (and_2_out, not_1_out, Gate);
  nor nor_1 (Q1_prime, Q1, S);
  nor nor_2 (Q1, R, Q1_prime);
  nand nand_1 (Q2_prime, Q2, R_2);
  nand nand_2 (Q2, S_2, Q2_prime);
  nor nor_3 (Q3_prime, Q3, and_1_out);
  nor nor_4 (Q3, and_2_out, Q3_prime);

  // Notes on the sheet:
  //   NOR Latch
  //   NAND Latch
  //   Gated D Latch
endmodule
