// Logisim project Lab_07_PT_09_Gray_Counter.circ as structural Verilog: 1 circuit, main circuit main
module main (
  input  Increment,
  input  Clock_Input,
  output Out_0,
  output Out_1
);

  wire and_1_out, and_2_out, and_3_out, and_4_out, and_5_out, and_6_out, d_ff_1_qn, not_1_out, or_1_out,
       or_2_out;

  D_Flip_Flop d_ff_1 (.clk(Clock_Input), .D(or_1_out), .Q(Out_1), .Qn(d_ff_1_qn));  // open: preset, en, reset
  D_Flip_Flop d_ff_2 (.clk(Clock_Input), .D(or_2_out), .Q(Out_0));  // open: Qn, preset, en, reset
  not not_1 (not_1_out, Increment);
  and and_1 (and_1_out, Increment, Out_0);
  and and_2 (and_2_out, not_1_out, Out_1);
  and and_3 (and_3_out, Out_1, Out_0);
  or or_1 (or_1_out, and_1_out, and_3_out, and_2_out);
  and and_4 (and_4_out, Increment, d_ff_1_qn);
  and and_5 (and_5_out, d_ff_1_qn, Out_0);
  or or_2 (or_2_out, and_4_out, and_5_out, and_6_out);
  and and_6 (and_6_out, not_1_out, Out_0);
endmodule
