// Logisim project Alarm_and_Fan-Replace.circ as structural Verilog: 1 circuit, main circuit main
module main (
  input  Cord,
  input  Low_Voltage,
  input  Temp,
  output Alarm,
  output Fan
);

  wire not_1_out, not_2_out, or_1_out;

  not not_1 (not_1_out, Low_Voltage);
  not not_2 (not_2_out, Cord);
  and and_1 (Alarm, not_2_out, Low_Voltage);
  or or_1 (or_1_out, Cord, not_1_out);
  and and_2 (Fan, or_1_out, Temp);
endmodule
