// Logisim project 13_sequential_circuits.circ as structural Verilog: 1 circuit, main circuit main
module main (
  input  D,
  input  W,
  output out_3,
  output out_4,
  output out_5,
  output out_6
);

  wire CLK_out, clock_1_out, clock_2_out, d_ff_3_q, d_ff_4_qn, multiplexer_1_out, not_1_out, xor_1_out;

  xor xor_1 (xor_1_out, out_6, out_3);
  not not_1 (not_1_out, out_6);
  Clock clock_1 (.out(clock_1_out));
  Multiplexer #(.enable("false")) multiplexer_1 (.in0(d_ff_3_q), .in1(D), .out(multiplexer_1_out), .sel(W));
  Clock CLK (.out(CLK_out));
  D_Flip_Flop d_ff_1 (.clk(clock_1_out), .D(xor_1_out), .Q(out_3));  // open: Qn, preset, en, reset
  D_Flip_Flop d_ff_2 (.clk(clock_1_out), .D(not_1_out), .Q(out_6));  // open: Qn, preset, en, reset
  D_Flip_Flop d_ff_3 (.clk(CLK_out), .D(multiplexer_1_out), .Q(d_ff_3_q));  // open: Qn, preset, en, reset
  Clock clock_2 (.out(clock_2_out));
  D_Flip_Flop d_ff_4 (.clk(clock_2_out), .D(out_5), .Q(out_4), .Qn(d_ff_4_qn));  // open: preset, en, reset
  D_Flip_Flop d_ff_5 (.clk(clock_2_out), .D(d_ff_4_qn), .Q(out_5));  // open: Qn, preset, en, reset

  // Notes on the sheet:
  //   Two-Bit Binary Counter
  //   1-Bit Loadable Register
  //   Two-Bit Gray Code Counter
endmodule
