// Logisim project L06_PT01_B.circ as structural Verilog: 1 circuit, main circuit main
module main (
  input  In0,
  input  In1,
  input  In2,
  input  In3,
  input  In4,
  input  In5,
  input  In6,
  input  In7,
  input  S2,
  input  S1,
  input  S0,
  output Out
);

  wire and_1_out, and_2_out, and_3_out, and_4_out, and_5_out, and_6_out, and_7_out, and_8_out, not_1_out,
       not_2_out, not_3_out, not_4_out, not_5_out, not_6_out, not_7_out, not_8_out;

  not not_1 (not_1_out, S2);
  not not_2 (not_2_out, not_3_out);
  not not_3 (not_3_out, not_4_out);
  not not_4 (not_4_out, S1);
  not not_5 (not_5_out, S0);
  not not_6 (not_6_out, S0);
  not not_7 (not_7_out, S0);
  not not_8 (not_8_out, S0);
  and and_1 (and_1_out, In0, not_1_out, not_2_out, not_5_out);
  and and_2 (and_2_out, In1, not_1_out, not_2_out, S0);
  and and_3 (and_3_out, In2, not_1_out, not_3_out, not_6_out);
  and and_4 (and_4_out, In3, not_1_out, not_3_out, S0);
  and and_5 (and_5_out, In4, S2, not_4_out, not_7_out);
  and and_6 (and_6_out, In5, S2, not_4_out, S0);
  and and_7 (and_7_out, In6, S2, S1, not_8_out);
  and and_8 (and_8_out, In7, S2, S1, S0);
  or or_1 (Out, and_1_out, and_2_out, and_3_out, and_4_out, and_5_out, and_6_out, and_7_out, and_8_out);
endmodule
