// Logisim project L11_PT01_B.circ as structural Verilog: 1 circuit, main circuit main
module main (
  input  Clr__A,
  input  Inc__B,
  input  Enable,
  output N1,
  output N0
);

  wire and_1_out, and_2_out, and_3_out, and_4_out, Clk_out, d_ff_1_qn, not_1_out, not_2_out, not_3_out,
       not_4_out, or_1_out, or_2_out;

  not not_1 (not_1_out, Clr__A);
  not not_2 (not_2_out, Inc__B);
  not not_3 (not_3_out, Clr__A);
  not not_4 (not_4_out, Inc__B);
  and and_1 (and_1_out, Inc__B, N0);
  or or_1 (or_1_out, and_1_out, and_2_out);
  and and_2 (and_2_out, not_1_out, not_2_out, N1);
  and and_3 (and_3_out, Inc__B, d_ff_1_qn);
  or or_2 (or_2_out, and_3_out, and_4_out);
  and and_4 (and_4_out, not_3_out, not_4_out, N0);
  Clock Clk (.out(Clk_out));
  D_Flip_Flop d_ff_1 (.clk(Clk_out), .D(or_1_out), .Q(N1), .Qn(d_ff_1_qn), .en(Enable));  // open: preset, reset
  D_Flip_Flop d_ff_2 (.clk(Clk_out), .D(or_2_out), .Q(N0), .en(Enable));  // open: Qn, preset, reset

  // Notes on the sheet:
  //   C
  //   D
endmodule
