// Logisim project LAB_01_Alarm_and_Fan-Replace.circ as structural Verilog: 1 circuit, main circuit main
module main (
  input  Cord,
  input  Low_Voltage,
  input  Temp,
  output Alarm,
  output Fan
);

  wire C_V_prime_out, not_1_out, not_2_out;

  not not_1 (not_1_out, Cord);
  not not_2 (not_2_out, Low_Voltage);
  and C_prime_V (Alarm, not_1_out, Low_Voltage);
  or C_V_prime (C_V_prime_out, Cord, not_2_out);
  and C_V_prime_T (Fan, C_V_prime_out, Temp);
endmodule
