// Logisim project Lab_03_PT_04_Road_Ripper.circ as structural Verilog: 1 circuit, main circuit main
module main (
  input  Stop,
  input  Left,
  input  Right,
  input  Clock,
  output L_Back,
  output R_Back,
  output L_Front,
  output R_Front
);

  wire and_1_out, and_2_out, and_3_out, and_4_out, not_1_out, not_2_out;

  not not_1 (not_1_out, Left);
  not not_2 (not_2_out, Right);
  and and_1 (and_1_out, Stop, not_1_out);
  and and_2 (and_2_out, Stop, not_2_out);
  and and_3 (and_3_out, Stop, Left);
  and and_4 (and_4_out, Stop, Right);
  and and_5 (L_Front, Left, Clock);
  and and_6 (R_Front, Right, Clock);
  or or_1 (L_Back, and_1_out, and_4_out, L_Front);
  or or_2 (R_Back, and_2_out, and_3_out, R_Front);
endmodule
