// Logisim project Lab_03_PT_05_Road_Ripper_ROM.circ as structural Verilog: 1 circuit, main circuit main
module main (
  input  Stop,
  input  Left,
  input  Right,
  input  Clock,
  output L_Front,
  output L_Back,
  output R_Front,
  output R_Back
);

  ROM #(.addrWidth(4), .dataWidth(4)) rom_1 (
    .addr({Stop, Left, Right, Clock}), .data({L_Front, L_Back, R_Front, R_Back}));  // open: sel

  // Notes on the sheet:
  //   contents of rom_1 (hex, n*v repeats v):
  //   0 0 0 3 0 c 0 f 5 5 4 7 1 d 5 f
endmodule
