// Logisim project RoadRipper-replace.circ as structural Verilog: 1 circuit, main circuit main
module main (
  input  Stop,
  input  Left,
  input  Right,
  input  Clock,
  output L_Front,
  output L_Back,
  output R_Front,
  output R_Back
);


  assign L_Back = Left;
  assign L_Front = Stop;
  assign R_Back = Clock;
  assign R_Front = Right;
endmodule
