// Logisim project 4bit_ALU-replace.circ as structural Verilog: 1 circuit, main circuit main
module main (
  input  A0,
  input  A1,
  input  A2,
  input  A3,
  input  B0,
  input  B1,
  input  B2,
  input  B3,
  input  S0,
  input  S1,
  output OUT_0,
  output OUT_1,
  output OUT_2,
  output OUT_3
);


  assign OUT_0 = A0;
  assign OUT_1 = A1;
  assign OUT_2 = A2;
  assign OUT_3 = A3;
endmodule
