// Logisim project Lab_04_PT_03_four_bit_adder.circ as structural Verilog: 2 circuits, main circuit main
module main (
  input  A0,
  input  in_2,
  input  B0,
  input  A1,
  input  B1,
  input  A2,
  input  B2,
  input  A3,
  input  B3,
  input  S0,
  input  S1,
  output OUT_0,
  output OUT_1,
  output OUT_2,
  output OUT_3
);

  wire full_adder_1_cout, full_adder_2_cout, full_adder_3_cout;

  Full_Adder full_adder_1 (.A(A0), .B(B0), .Sum(OUT_0), .Cout(full_adder_1_cout), .Cin(in_2));
  Full_Adder full_adder_2 (.A(A1), .B(B1), .Sum(OUT_1), .Cout(full_adder_2_cout), .Cin(full_adder_1_cout));
  Full_Adder full_adder_3 (.A(A2), .B(B2), .Sum(OUT_2), .Cout(full_adder_3_cout), .Cin(full_adder_2_cout));
  Full_Adder full_adder_4 (.A(A3), .B(B3), .Sum(OUT_3), .Cin(full_adder_3_cout));  // open: Cout
endmodule

module Full_Adder (
  input  A,
  input  B,
  input  Cin,
  output Sum,
  output Cout
);

  wire and_1_out, and_2_out, and_3_out;

  xor xor_1 (Sum, A, B, Cin);
  and and_1 (and_1_out, B, A);
  and and_2 (and_2_out, B, Cin);
  and and_3 (and_3_out, A, Cin);
  or or_1 (Cout, and_1_out, and_2_out, and_3_out);
endmodule
