// Logisim project TwoBit_2to1_MUX-replace.circ as structural Verilog: 1 circuit, main circuit main
module main (
  input  A0,
  input  A1,
  input  B0,
  input  B1,
  input  S,
  output D0,
  output D1
);


  assign D0 = A0;
  assign D1 = A1;
endmodule
