// Logisim project 4bit_8word_Reg-replace.circ as structural Verilog: 1 circuit, main circuit main
module main (
  input  In_0,
  input  In_1,
  input  In_2,
  input  In_3,
  input  Clock_input,
  input  A0,
  input  A1,
  input  A2,
  input  WE,
  output OUT_0,
  output OUT_1,
  output OUT_2,
  output OUT_3
);


  assign OUT_0 = A1;
  assign OUT_1 = A0;
  assign OUT_2 = WE;
  assign OUT_3 = A2;
endmodule
