// Logisim project Lab_06_PT_02_4bit_8word_Reg_refactor.circ as structural Verilog: 4 circuits, main circuit main
module main (
  input  In_0,
  input  In_1,
  input  In_2,
  input  In_3,
  input  Clock_input,
  input  A0,
  input  A1,
  input  A2,
  input  WE,
  output OUT_0,
  output OUT_1,
  output OUT_2,
  output OUT_3
);

  wire write_decoder_1__000, write_decoder_1__001, write_decoder_1__010, write_decoder_1__011,
       write_decoder_1__100, write_decoder_1__101, write_decoder_1__110, write_decoder_1__111;
  wire [3:0] n4_bit_register_1_out_4, n4_bit_register_2_out_4, n4_bit_register_3_out_4,
       n4_bit_register_4_out_4, n4_bit_register_5_out_4, n4_bit_register_6_out_4, n4_bit_register_7_out_4,
       n4_bit_register_8_out_4;

  Write_Decoder write_decoder_1 (
    .A0(A0), .A1(A1), .A2(A2), ._000(write_decoder_1__000), ._001(write_decoder_1__001),
    ._010(write_decoder_1__010), ._011(write_decoder_1__011), ._100(write_decoder_1__100),
    ._101(write_decoder_1__101), ._110(write_decoder_1__110), ._111(write_decoder_1__111), .WE(WE));
  _4_bit_Register u_4_bit_register_1 (
    .WE(write_decoder_1__000), .Clock(Clock_input), .in_1({In_3, In_2, In_1, In_0}),
    .out_4(n4_bit_register_1_out_4));
  _4_bit_Register u_4_bit_register_2 (
    .WE(write_decoder_1__010), .Clock(Clock_input), .in_1({In_3, In_2, In_1, In_0}),
    .out_4(n4_bit_register_2_out_4));
  _4_bit_Register u_4_bit_register_3 (
    .WE(write_decoder_1__100), .Clock(Clock_input), .in_1({In_3, In_2, In_1, In_0}),
    .out_4(n4_bit_register_3_out_4));
  _4_bit_Register u_4_bit_register_4 (
    .WE(write_decoder_1__110), .Clock(Clock_input), .in_1({In_3, In_2, In_1, In_0}),
    .out_4(n4_bit_register_4_out_4));
  _4_bit_Register u_4_bit_register_5 (
    .WE(write_decoder_1__001), .Clock(Clock_input), .in_1({In_3, In_2, In_1, In_0}),
    .out_4(n4_bit_register_5_out_4));
  _4_bit_Register u_4_bit_register_6 (
    .WE(write_decoder_1__011), .Clock(Clock_input), .in_1({In_3, In_2, In_1, In_0}),
    .out_4(n4_bit_register_6_out_4));
  _4_bit_Register u_4_bit_register_7 (
    .WE(write_decoder_1__101), .Clock(Clock_input), .in_1({In_3, In_2, In_1, In_0}),
    .out_4(n4_bit_register_7_out_4));
  _4_bit_Register u_4_bit_register_8 (
    .WE(write_decoder_1__111), .Clock(Clock_input), .in_1({In_3, In_2, In_1, In_0}),
    .out_4(n4_bit_register_8_out_4));
  Multiplexer #(.select(3), .width(4), .enable("false")) multiplexer_1 (
    .in0(n4_bit_register_1_out_4), .in1(n4_bit_register_5_out_4), .in2(n4_bit_register_2_out_4),
    .in3(n4_bit_register_6_out_4), .in4(n4_bit_register_3_out_4), .in5(n4_bit_register_7_out_4),
    .in6(n4_bit_register_4_out_4), .in7(n4_bit_register_8_out_4), .out({OUT_3, OUT_2, OUT_1, OUT_0}),
    .sel({A2, A1, A0}));
endmodule

module Write_Decoder (
  input  A0,
  input  A1,
  input  A2,
  input  WE,
  output _000,
  output _001,
  output _010,
  output _011,
  output _100,
  output _101,
  output _110,
  output _111
);

  wire not_1_out, not_2_out, not_3_out;

  not not_1 (not_1_out, A0);
  not not_2 (not_2_out, A1);
  not not_3 (not_3_out, A2);
  and and_1 (_000, not_3_out, not_2_out, not_1_out, WE);
  and and_2 (_001, not_3_out, not_2_out, A0, WE);
  and and_3 (_010, not_3_out, A1, not_1_out, WE);
  and and_4 (_011, not_3_out, A1, A0, WE);
  and and_5 (_100, A2, not_2_out, not_1_out, WE);
  and and_6 (_101, A2, not_2_out, A0, WE);
  and and_7 (_110, A2, A1, not_1_out, WE);
  and and_8 (_111, A2, A1, A0, WE);
endmodule

module _1_bit_Register (
  input  D,
  input  WE,
  input  Clock,
  output Q
);

  wire multiplexer_1_out;

  Multiplexer #(.enable("false")) multiplexer_1 (.in0(Q), .in1(D), .out(multiplexer_1_out), .sel(WE));
  D_Flip_Flop d_ff_1 (.clk(Clock), .D(multiplexer_1_out), .Q(Q));  // open: Qn, preset, en, reset
endmodule

module _4_bit_Register (
  input  [3:0] in_1,
  input  WE,
  input  Clock,
  output [3:0] out_4
);

  _1_bit_Register u_1_bit_register_1 (.D(in_1[0]), .Q(out_4[0]), .WE(WE), .Clock(Clock));
  _1_bit_Register u_1_bit_register_2 (.D(in_1[1]), .Q(out_4[1]), .WE(WE), .Clock(Clock));
  _1_bit_Register u_1_bit_register_3 (.D(in_1[2]), .Q(out_4[2]), .WE(WE), .Clock(Clock));
  _1_bit_Register u_1_bit_register_4 (.D(in_1[3]), .Q(out_4[3]), .WE(WE), .Clock(Clock));
endmodule
