// Logisim project Graycode_2b_Counter-replace.circ as structural Verilog: 1 circuit, main circuit main
module main (
  input  Increment,
  input  Clock_Input,
  output Out_0,
  output Out_1
);


  assign Out_0 = Increment;
  assign Out_1 = Increment;
endmodule
