// Logisim project Lab_07_PT_03_Up_Counter_refactor.circ as structural Verilog: 1 circuit, main circuit main
module main (
  input  Clock_Input,
  output Out_0,
  output Out_1,
  output Out_2
);

  wire d_ff_1_qn, d_ff_2_qn, d_ff_3_qn, nand_1_out, nand_2_out, nand_3_out, nand_4_out, nand_5_out,
       nand_6_out, nand_7_out;

  nand nand_1 (nand_1_out, nand_2_out, nand_3_out, nand_4_out);
  nand nand_2 (nand_2_out, Out_2, d_ff_2_qn);
  nand nand_3 (nand_3_out, d_ff_3_qn, Out_2);
  nand nand_4 (nand_4_out, d_ff_1_qn, Out_1, Out_0);
  D_Flip_Flop d_ff_1 (.clk(Clock_Input), .D(nand_1_out), .Q(Out_2), .Qn(d_ff_1_qn));  // open: preset, en, reset
  nand nand_5 (nand_5_out, nand_6_out, nand_7_out);
  D_Flip_Flop d_ff_2 (.clk(Clock_Input), .D(nand_5_out), .Q(Out_1), .Qn(d_ff_2_qn));  // open: preset, en, reset
  nand nand_6 (nand_6_out, Out_1, d_ff_3_qn);
  nand nand_7 (nand_7_out, d_ff_2_qn, Out_0);
  D_Flip_Flop d_ff_3 (.clk(Clock_Input), .D(d_ff_3_qn), .Q(Out_0), .Qn(d_ff_3_qn));  // open: preset, en, reset
endmodule
