// Logisim project gated_SR_latch.circ as structural Verilog: 1 circuit, main circuit main
module main (
  input  D,
  input  S,
  input  R,
  input  Gate,
  input  S_2,
  input  in_6,
  input  R_2,
  input  in_8,
  input  in_9,
  input  in_10,
  input  in_11,
  input  in_12,
  input  in_13,
  input  D_2,
  input  Gate_2,
  output Q_prime,
  output Q_prime_2,
  output Q,
  output Q_2,
  output Q_3,
  output out_21,
  output out_22,
  output Q_prime_3,
  output out_24,
  output Q_prime_4,
  output Q_4
);

  wire and_1_out, and_2_out, and_3_out, and_4_out, and_5_out, and_6_out, clock_1_out, clock_2_out, d_ff_2_q,
       nor_3_out, nor_4_out, not_1_out, not_2_out, not_3_out, not_4_out;

  not not_1 (not_1_out, D_2);
  nor nor_1 (Q_prime, Q, S);
  nor nor_2 (Q, R, Q_prime);
  nand nand_1 (Q_3, Q_prime_3, S_2);
  nand nand_2 (Q_prime_3, R_2, Q_3);
  and and_1 (and_1_out, D_2, Gate_2);
  and and_2 (and_2_out, not_1_out, Gate_2);
  nor nor_3 (nor_3_out, nor_4_out, and_1_out);
  nor nor_4 (nor_4_out, and_2_out, nor_3_out);
  not not_2 (not_2_out, Gate_2);
  not not_3 (not_3_out, D);
  Clock clock_1 (.out(clock_1_out));
  and and_3 (and_3_out, nor_3_out, not_2_out);
  and and_4 (and_4_out, not_2_out, nor_4_out);
  nor nor_5 (Q_prime_2, Q_2, and_5_out);
  and and_5 (and_5_out, D, Gate);
  and and_6 (and_6_out, not_3_out, Gate);
  nor nor_6 (Q_2, and_6_out, Q_prime_2);
  D_Flip_Flop d_ff_1 (.clk(clock_1_out), .D(in_6), .Q(out_21), .Qn(out_22), .preset(in_8), .en(in_9), .reset(in_10));
  nor nor_7 (Q_prime_4, Q_4, and_3_out);
  nor nor_8 (Q_4, and_4_out, Q_prime_4);
  not not_4 (not_4_out, d_ff_2_q);
  D_Flip_Flop d_ff_2 (
    .clk(clock_2_out), .D(not_4_out), .Q(d_ff_2_q), .Qn(out_24), .preset(in_11), .en(in_12), .reset(in_13));
  Clock clock_2 (.out(clock_2_out));
endmodule
